# Fritzing sketch Working Model (saved by Fritzing 0.9.3b)
circuit board: 8.46667cm x 5.64444cm
breadboards: 1

parts:
  U1 = NodeMCU V3.0
  ADC1 = MCP3008 [package=dil16]
  Part1 = Ambient Light Sensor (TEMT6000 Breakout Board)
  AM1 = AM2302 Humidity and Temperature Sensor

nets:
  N1: U1.D2, AM1.DATA
  VDD: U1.3V3, ADC1.VREF, ADC1.VDD, Part1.VCC, AM1.VDD
  GND: U1.GND#6, U1.GND#13, U1.GND#16, U1.GND#33, ADC1.DGND, ADC1.AGND, Part1.GND, AM1.GND
  N2: U1.D5, ADC1.CLK
  N3: U1.D6, ADC1.Dout
  N4: U1.D7, ADC1.Din
  N5: U1.D8, ADC1.CS/SHDN
  N6: ADC1.CH0, Part1.S

custom parts:
  NodeMCU V3.0: ESP8266 based NodeMCU
